// Logisim project F1.circ as structural Verilog: 1 circuit, main circuit main
module main (
  input  [2:0] A,
  input  [2:0] B,
  input  [2:0] C,
  output [4:0] out_4
);

  wire [2:0] adder_1_out;
  wire [3:0] bit_extender_1_out;
  wire [3:3] adder_1_cout;

  Adder #(.width(3)) adder_1 (.a(A), .b(B), .out(adder_1_out), .cout(adder_1_cout[3]));  // open: cin
  assign bit_extender_1_out = {{1{1'b0}}, C};  // Bit_Extender bit_extender_1
  Adder #(.width(4)) adder_2 (
    .a({adder_1_cout[3], adder_1_out}), .b(bit_extender_1_out), .out(out_4[3:0]), .cout(out_4[4]));  // open: cin

  // Notes on the sheet:
  //   F1=A+B+C
endmodule
