// Logisim project F2.circ as structural Verilog: 1 circuit, main circuit main
module main (
  input  [2:0] A,
  input  [2:0] B,
  input  [2:0] C,
  output [3:0] out_4,
  output out_5
);

  wire [2:0] subtractor_1_out;
  wire [3:0] bit_extender_1_out;
  wire [3:3] subtractor_1_bout;

  Subtractor #(.width(3)) subtractor_1 (
    .a(A), .b(B), .out(subtractor_1_out), .bout(subtractor_1_bout[3]));  // open: bin
  assign bit_extender_1_out = {{1{1'b0}}, C};  // Bit_Extender bit_extender_1
  Subtractor #(.width(4)) subtractor_2 (
    .a({subtractor_1_bout[3], subtractor_1_out}), .b(bit_extender_1_out), .out(out_4), .bout(out_5));  // open: bin

  // Notes on the sheet:
  //   F2=A-B-C
endmodule
