// Logisim project F3.circ as structural Verilog: 1 circuit, main circuit main
module main (
  input  [2:0] B,
  input  in_2,
  output [3:0] out_3
);

  wire [2:0] bit_extender_1_out, not_1_out;

  not not_1 (not_1_out[0], B[0]);
  not not_2 (not_1_out[1], B[1]);
  not not_3 (not_1_out[2], B[2]);
  assign bit_extender_1_out = {{2{1'b0}}, in_2};  // Bit_Extender bit_extender_1
  Adder #(.width(3)) adder_1 (.a(not_1_out), .b(bit_extender_1_out), .out(out_3[2:0]), .cout(out_3[3]));  // open: cin

  // Notes on the sheet:
  //   2's complement
endmodule
