// Logisim project F4.circ as structural Verilog: 1 circuit, main circuit main
module main (
  input  [1:0] in_1,
  input  [2:0] A,
  input  [2:0] B,
  input  [2:0] C,
  output [4:0] out_5
);

  wire [2:0] adder_1_out, shifter_1_out;
  wire [3:0] bit_extender_1_out;
  wire [3:3] adder_1_cout;

  Shifter #(.width(3), .shift("lr")) shifter_1 (.in(A), .\dist (in_1), .out(shifter_1_out));
  Adder #(.width(3)) adder_1 (.a(B), .b(C), .out(adder_1_out), .cout(adder_1_cout[3]));  // open: cin
  assign bit_extender_1_out = {{1{1'b0}}, shifter_1_out};  // Bit_Extender bit_extender_1
  Adder #(.width(4)) adder_2 (
    .a(bit_extender_1_out), .b({adder_1_cout[3], adder_1_out}), .out(out_5[3:0]), .cout(out_5[4]));  // open: cin

  // Notes on the sheet:
  //   F=A/2+B+C
endmodule
