// Logisim project final part 3.circ as structural Verilog: 1 circuit, main circuit main
module main (
  input  in_1,
  input  [4:0] in_2,
  input  [1:0] in_3,
  input  [1:0] in_4
);

  wire [2:0] adder_1_out, adder_2_out, adder_3_out, adder_5_out, bit_extender_1_out, bit_extender_2_out,
       bit_extender_3_out, bit_extender_6_out, not_1_out, shifter_1_out, shifter_2_out, subtractor_1_out;
  wire [3:0] adder_4_out, adder_7_out, bit_extender_4_out, bit_extender_5_out, bit_extender_7_out,
       bit_extender_8_out, counter_1_q, subtractor_2_out;
  wire [3:3] adder_1_cout, adder_2_cout, adder_3_cout, adder_5_cout, subtractor_1_bout;
  wire [4:0] adder_6_out, bit_extender_9_out, multiplexer_1_out;
  wire [4:4] adder_4_cout, adder_7_cout, subtractor_2_bout;
  wire [5:0] bit_extender_10_out;
  wire [15:0] rom_1_data, rom_2_data, rom_3_data, rom_4_data;

  Counter #(.width(4), .max('hf)) counter_1 (.Q(counter_1_q));  // open: load, D, count, carry, clk, clr
  ROM #(.addrWidth(4), .dataWidth(16)) rom_1 (.addr(counter_1_q), .data(rom_1_data));  // open: sel
  ROM #(.addrWidth(4), .dataWidth(16)) rom_2 (.addr(counter_1_q), .data(rom_2_data));  // open: sel
  ROM #(.addrWidth(4), .dataWidth(16)) rom_3 (.addr(counter_1_q), .data(rom_3_data));  // open: sel
  ROM #(.addrWidth(4), .dataWidth(16)) rom_4 (.addr(counter_1_q), .data(rom_4_data));  // open: sel
  Bit_Extender #(.in_width(16), .out_width(3)) bit_extender_1 (.in(rom_1_data), .out(bit_extender_1_out));
  Bit_Extender #(.in_width(16), .out_width(3)) bit_extender_2 (.in(rom_2_data), .out(bit_extender_2_out));
  Bit_Extender #(.in_width(16), .out_width(3)) bit_extender_3 (.in(rom_3_data), .out(bit_extender_3_out));
  assign bit_extender_4_out = {{1{1'b0}}, bit_extender_3_out};  // Bit_Extender bit_extender_4
  Shifter #(.width(3)) shifter_1 (.in(bit_extender_1_out), .\dist (in_4), .out(shifter_1_out));
  Adder #(.width(3)) adder_1 (
    .a(bit_extender_2_out), .b(bit_extender_3_out), .out(adder_1_out), .cout(adder_1_cout[3]));  // open: cin
  Adder #(.width(3)) adder_2 (
    .a(bit_extender_1_out), .b(bit_extender_2_out), .out(adder_2_out), .cout(adder_2_cout[3]));  // open: cin
  assign bit_extender_5_out = {{1{1'b0}}, bit_extender_3_out};  // Bit_Extender bit_extender_5
  Subtractor #(.width(3)) subtractor_1 (
    .a(bit_extender_1_out), .b(bit_extender_2_out), .out(subtractor_1_out), .bout(subtractor_1_bout[3]));  // open: bin
  not not_1 (not_1_out[0], bit_extender_2_out[0]);
  not not_2 (not_1_out[1], bit_extender_2_out[1]);
  not not_3 (not_1_out[2], bit_extender_2_out[2]);
  Shifter #(.width(3), .shift("lr")) shifter_2 (.in(bit_extender_1_out), .\dist (in_3), .out(shifter_2_out));
  Adder #(.width(3)) adder_3 (
    .a(bit_extender_2_out), .b(bit_extender_3_out), .out(adder_3_out), .cout(adder_3_cout[3]));  // open: cin
  assign bit_extender_6_out = {{2{1'b0}}, in_1};  // Bit_Extender bit_extender_6
  assign bit_extender_7_out = {{1{1'b0}}, shifter_2_out};  // Bit_Extender bit_extender_7
  assign bit_extender_8_out = {{1{1'b0}}, shifter_1_out};  // Bit_Extender bit_extender_8
  Adder #(.width(4)) adder_4 (
    .a({adder_2_cout[3], adder_2_out}), .b(bit_extender_5_out), .out(adder_4_out), .cout(adder_4_cout[4]));  // open: cin
  Subtractor #(.width(4)) subtractor_2 (
    .a({subtractor_1_bout[3], subtractor_1_out}), .b(bit_extender_4_out), .out(subtractor_2_out),
    .bout(subtractor_2_bout[4]));  // open: bin
  Adder #(.width(3)) adder_5 (
    .a(not_1_out), .b(bit_extender_6_out), .out(adder_5_out), .cout(adder_5_cout[3]));  // open: cin
  Adder #(.width(4)) adder_6 (
    .a(bit_extender_7_out), .b({adder_3_cout[3], adder_3_out}), .out(adder_6_out[3:0]), .cout(adder_6_out[4]));  // open: cin
  Adder #(.width(4)) adder_7 (
    .a(bit_extender_8_out), .b({adder_1_cout[3], adder_1_out}), .out(adder_7_out), .cout(adder_7_cout[4]));  // open: cin
  assign bit_extender_9_out = {{1{1'b0}}, {adder_5_cout[3], adder_5_out}};  // Bit_Extender bit_extender_9
  Multiplexer #(.select(5), .width(5)) multiplexer_1 (
    .in0({adder_4_cout[4], adder_4_out}), .in7({subtractor_2_bout[4], subtractor_2_out}),
    .in8({subtractor_2_bout[4], subtractor_2_out}), .in9({subtractor_2_bout[4], subtractor_2_out}),
    .in11(bit_extender_9_out), .in12(bit_extender_9_out), .in16(adder_6_out),
    .in29({adder_7_cout[4], adder_7_out}), .out(multiplexer_1_out), .sel(in_2));  // open: in1, in2, in3, in4, in5, in6, in10, in13, in14, in15, in17, in18, in19, in20, in21, in22, in23, in24, in25, in26, in27, in28, in30, in31, en
  assign bit_extender_10_out = {{1{1'b0}}, multiplexer_1_out};  // Bit_Extender bit_extender_10
  RAM #(.addrWidth(16), .dataWidth(6)) ram_1 (
    .addr(rom_4_data), .data(bit_extender_10_out));  // open: sel, clk, ld, clr

  // Notes on the sheet:
  //   F5=A*4+B+C
endmodule
