// Logisim project part 2 final.circ as structural Verilog: 1 circuit, main circuit main
module main (
  input  [2:0] A,
  input  [2:0] B,
  input  [2:0] C,
  input  [2:0] A_2,
  input  [2:0] B_2,
  input  [2:0] C_2,
  input  [1:0] in_7,
  input  [2:0] A_3,
  input  [2:0] B_3,
  input  [2:0] C_3,
  input  [2:0] in_11,
  input  [2:0] B_4,
  input  in_13,
  input  [2:0] A_4,
  input  [1:0] in_15,
  input  [2:0] B_5,
  input  [2:0] C_4,
  output [4:0] out_18
);

  wire [2:0] adder_1_out, adder_2_out, adder_3_out, adder_4_out, bit_extender_3_out, not_2_out,
       shifter_1_out, shifter_2_out, subtractor_1_out;
  wire [3:0] adder_5_out, adder_6_out, adder_7_out, bit_extender_1_out, bit_extender_2_out,
       bit_extender_4_out, bit_extender_5_out, subtractor_2_out;
  wire [3:3] adder_1_cout, adder_2_cout, adder_3_cout, adder_4_cout, subtractor_1_bout;
  wire [4:0] bit_extender_6_out;
  wire [4:4] adder_5_cout, adder_6_cout, adder_7_cout, subtractor_2_bout;

  not not_1 (not_2_out[2], B_4[2]);
  Adder #(.width(3)) adder_1 (.a(A), .b(B), .out(adder_1_out), .cout(adder_1_cout[3]));  // open: cin
  assign bit_extender_1_out = {{1{1'b0}}, C};  // Bit_Extender bit_extender_1
  Subtractor #(.width(3)) subtractor_1 (
    .a(A_2), .b(B_2), .out(subtractor_1_out), .bout(subtractor_1_bout[3]));  // open: bin
  assign bit_extender_2_out = {{1{1'b0}}, C_2};  // Bit_Extender bit_extender_2
  Shifter #(.width(3), .shift("lr")) shifter_1 (.in(A_3), .\dist (in_7), .out(shifter_1_out));
  Adder #(.width(3)) adder_2 (.a(B_3), .b(C_3), .out(adder_2_out), .cout(adder_2_cout[3]));  // open: cin
  not not_2 (not_2_out[0], B_4[0]);
  not not_3 (not_2_out[1], B_4[1]);
  assign bit_extender_3_out = {{2{1'b0}}, in_13};  // Bit_Extender bit_extender_3
  Shifter #(.width(3)) shifter_2 (.in(A_4), .\dist (in_15), .out(shifter_2_out));
  Adder #(.width(3)) adder_3 (.a(B_5), .b(C_4), .out(adder_3_out), .cout(adder_3_cout[3]));  // open: cin
  assign bit_extender_4_out = {{1{1'b0}}, shifter_2_out};  // Bit_Extender bit_extender_4
  assign bit_extender_5_out = {{1{1'b0}}, shifter_1_out};  // Bit_Extender bit_extender_5
  Adder #(.width(3)) adder_4 (
    .a(not_2_out), .b(bit_extender_3_out), .out(adder_4_out), .cout(adder_4_cout[3]));  // open: cin
  Adder #(.width(4)) adder_5 (
    .a({adder_1_cout[3], adder_1_out}), .b(bit_extender_1_out), .out(adder_5_out), .cout(adder_5_cout[4]));  // open: cin
  Subtractor #(.width(4)) subtractor_2 (
    .a({subtractor_1_bout[3], subtractor_1_out}), .b(bit_extender_2_out), .out(subtractor_2_out),
    .bout(subtractor_2_bout[4]));  // open: bin
  Adder #(.width(4)) adder_6 (
    .a(bit_extender_5_out), .b({adder_2_cout[3], adder_2_out}), .out(adder_6_out), .cout(adder_6_cout[4]));  // open: cin
  assign bit_extender_6_out = {{1{1'b0}}, {adder_4_cout[3], adder_4_out}};  // Bit_Extender bit_extender_6
  Adder #(.width(4)) adder_7 (
    .a(bit_extender_4_out), .b({adder_3_cout[3], adder_3_out}), .out(adder_7_out), .cout(adder_7_cout[4]));  // open: cin
  Multiplexer #(.select(3), .width(5)) multiplexer_1 (
    .in0({adder_5_cout[4], adder_5_out}), .in1({subtractor_2_bout[4], subtractor_2_out}),
    .in2({adder_6_cout[4], adder_6_out}), .in3(bit_extender_6_out), .in4({adder_7_cout[4], adder_7_out}),
    .out(out_18), .sel(in_11));  // open: in5, in6, in7, en

  // Notes on the sheet:
  //   F1=A+B+C
  //   F2=A-B-C
  //   F4 = 2's Complement of B
  //   F5=A*4+B+C
  //   F=A/2+B+C
endmodule
